# Fritzing sketch 01_Servo_ItsyBitsy (saved by Fritzing 0.9.4)
breadboards: 1

parts:
  Part1 = Itsy Bitsy 32u4 5V @ 16MHz [part_number="Adafruit #3677"]  # not connected
  M1 = Dagu DGServo 9g (Top view) [part_number=RS001B]
  M2 = Dagu DGServo 9g (Top view) [part_number=RS001B]
  S1 = Pushbutton [package="[THT]"]

nets:
  GND: M1.gnd, M2.gnd, S1.Pin_1, S1.Pin_2
  VCC: M1.vcc, M2.vcc
  N1: S1.Pin_3, S1.Pin_4

custom parts:
  Itsy Bitsy 32u4 5V @ 16MHz: What's smaller than a Feather but larger than a Trinket? It's an Itsy Bitsy! Small, powerful, Arduino-compatible - this microcontroller board is perfect when you want something very compact, but still with a bunch of pins. Itsy Bitsy is only 1.4" long by 0.7" wide, but has 6 power pins, 6 analog & digital pins and 17 digital pins. It packs much of the same capability as an Arduino UNO. So it's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
