# Fritzing sketch 01_Wizard_of_Oz (saved by Fritzing 0.9.9b)
breadboards: 2

parts:
  Part1 = Itsy Bitsy 32u4 5V @ 16MHz [part_number="Adafruit #3677"]
  SERVO1 = Tower Pro SG90 servo [part_number=101246]
  R2 = Trimmer Potentiometer [maximum_resistance=10kΩ package=THT]

nets:
  GND: Part1.GND, SERVO1.GND, R2.leg2
  N1: Part1.D10, SERVO1.Signal
  N2: Part1.A3, R2.wiper
  +5V: Part1.+5V, SERVO1.+5V, R2.leg1

custom parts:
  Itsy Bitsy 32u4 5V @ 16MHz: What's smaller than a Feather but larger than a Trinket? It's an Itsy Bitsy! Small, powerful, Arduino-compatible - this microcontroller board is perfect when you want something very compact, but still with a bunch of pins. Itsy Bitsy is only 1.4" long by 0.7" wide, but has 6 power pins, 6 analog & digital pins and 17 digital pins. It packs much of the same capability as an Arduino UNO. So it's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
  Tower Pro SG90 servo: Original file by John De Cristofaro http://www.adafruit.com/products/1449 Adafruit Feedback Servo (Small) Edited by: e-radionica.com 28/9/2015
