# Fritzing sketch 02_Servo_ESP32 (saved by Fritzing 0.9.4)

parts:
  M2 = Dagu DGServo 9g (Top view) [part_number=RS001B]
  U1 = ESP32-38PinWide [part_number=ESP32-38PinWide]

nets:
  GND: M2.gnd, U1.GND
  VCC: M2.vcc, U1.VIN
  N1: M2.pulse, U1.GPIO18

custom parts:
  ESP32-38PinWide: Generic 38-Pin ESP32 with wide format (only access to one side of pins on a breadboard) based on Stephen Lilley's HiLetgo ESP-WROOM-32 ESP32 ESP-32S Development Board.
