# Fritzing sketch 04_Multiple_Servos_ItsyBitsy (saved by Fritzing 0.9.9b)
breadboards: 1

parts:
  Part1 = Itsy Bitsy 32u4 5V @ 16MHz [part_number="Adafruit #3677"]
  SERVO1 = Tower Pro SG90 servo [part_number=101246]
  YwRobot_Power_Supply1 = YwRobot Breadboard Power Supply [part_number=545043]
  SERVO2 = Tower Pro SG90 servo [part_number=101246]
  SERVO3 = Tower Pro SG90 servo [part_number=101246]

nets:
  +5V: Part1.VBAT, SERVO1.+5V, YwRobot_Power_Supply1.VCC#5, YwRobot_Power_Supply1.VCC#6, SERVO2.+5V, SERVO3.+5V
  GND: Part1.GND, SERVO1.GND, YwRobot_Power_Supply1.GND#11, YwRobot_Power_Supply1.GND#12, SERVO2.GND, SERVO3.GND
  N1: Part1.D11, SERVO3.Signal
  N2: Part1.D10, SERVO2.Signal
  N3: Part1.D5, SERVO1.Signal
  N4: YwRobot_Power_Supply1.VCC#9, YwRobot_Power_Supply1.VCC#10
  N5: YwRobot_Power_Supply1.GND#13, YwRobot_Power_Supply1.GND#14

custom parts:
  Itsy Bitsy 32u4 5V @ 16MHz: What's smaller than a Feather but larger than a Trinket? It's an Itsy Bitsy! Small, powerful, Arduino-compatible - this microcontroller board is perfect when you want something very compact, but still with a bunch of pins. Itsy Bitsy is only 1.4" long by 0.7" wide, but has 6 power pins, 6 analog & digital pins and 17 digital pins. It packs much of the same capability as an Arduino UNO. So it's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
  Tower Pro SG90 servo: Original file by John De Cristofaro http://www.adafruit.com/products/1449 Adafruit Feedback Servo (Small) Edited by: e-radionica.com 28/9/2015
  YwRobot Breadboard Power Supply: The YwRobot Breadboard Power Supply (MB-V2) has two power rails; they can be 5V or 3V3. Power to the module can be provided through the female USB socket or through the A10 (female) 2.1mm power jack.
